# Fritzing sketch mkr-tmp36-sensor-circuit-diagram (saved by Fritzing 0.9.4)
breadboards: 1

parts:
  Part1 = Arduino MKR WiFi 1010
  T1 = TMP36 Temperature Sensor [package="TO92 [THT]"]

nets:
  N1: Part1.A0_DAC0, T1.Vout
  GND: Part1.GND, T1.GND
  N2: Part1.VCC, T1.+Vs

custom parts:
  Arduino MKR WiFi 1010: This is the newest version of the MKR 1000 WIFI, but with an ESP32 module on board made by U-BLOX.
