# Fritzing sketch uno-tmp36-sensor-circuit-diagram (saved by Fritzing 0.9.4)
breadboards: 1

parts:
  Part2 = Arduino Uno (Rev3)
  T1 = TMP36 Temperature Sensor [package="TO92 [THT]"]

nets:
  N1: Part2.A0, T1.Vout
  GND: Part2.GND, T1.GND
  N2: Part2.5V, T1.+Vs
