# Fritzing sketch esp32-tmp36-sensor-circuit-diagram (saved by Fritzing 0.9.4)
breadboards: 1

parts:
  MCU1 = Wemos Lolin32lite
  T1 = TMP36 Temperature Sensor [package="TO92 [THT]"]

nets:
  N1: MCU1.pin_4, T1.Vout
  N2: MCU1.pin_13, T1.GND
  N3: MCU1.pin_28, T1.+Vs

custom parts:
  Wemos Lolin32lite: Wemos Lolinlite32 wifi and bluetooth board based on the ESP-32 cpu, digital I/Os 19, analog inputs 6, clock 240mhz, Flash 4Mbytes, lipo battery charger (500ma connection broken out on breadboard but not pcb), usb.
