# Fritzing sketch esp8266-tmp36-sensor-circuit-diagram (saved by Fritzing 0.9.4)
breadboards: 1

parts:
  WeMos_D1_Mini1 = WeMos D1 Mini
  T1 = TMP36 Temperature Sensor [package="TO92 [THT]"]

nets:
  N1: WeMos_D1_Mini1.3V3, T1.+Vs
  N2: WeMos_D1_Mini1.A0, T1.Vout
  N3: WeMos_D1_Mini1.G, T1.GND
